# Fritzing sketch design-all (saved by Fritzing 0.9.6b)
breadboards: 1

parts:
  Part1 = Arduino Uno (Rev3)
  Part2 = MQ-7 breakout
  RHT3 = Humidity and Temperature Sensor RHT03
  R3 = Resistor [tolerance=±5% resistance=10k package="0603 [SMD]"]
  Part3 = MQ-7 breakout
  YL-83_-_Detection_Board2 = YL-83 Rain Sensor - Detection Board
  YL-83_-_Control_Board2 = YL-83 Rain Sensor - Control Board
  Capacitive_Soil_Moisture_Sensor1 = DFRobot Capacitive Soil Moisture Sensor V1.0 [part_number=SEN0193]

nets:
  N1: Part1.A0, Part3.AO
  N2: Part1.A1, Part2.AO
  N3: Part1.A2, YL-83_-_Control_Board2.AO
  N4: Part1.A3, Capacitive_Soil_Moisture_Sensor1.A
  N5: Part1.D7, RHT3.GND_1
  3V3: Part1.3V3, Capacitive_Soil_Moisture_Sensor1.VCC
  VCC: Part1.5V, Part2.VCC, RHT3.Vcc, R3.Pin_0, Part3.VCC, YL-83_-_Control_Board2.VCC
  GND: Part1.GND, Part2.GND, RHT3.GND_2, Part3.GND, YL-83_-_Control_Board2.GND, Capacitive_Soil_Moisture_Sensor1.GND
  N6: RHT3.Data-signal, R3.Pin_1
  N7: YL-83_-_Detection_Board2.POS, YL-83_-_Control_Board2.POS
  N8: YL-83_-_Detection_Board2.NEG, YL-83_-_Control_Board2.NEG

notes:
  MQ-135

custom parts:
  MQ-7 breakout: SKU: 101282
  YL-83 Rain Sensor - Detection Board: The YL-83 is a rain sensor that has more resistance when dry and less resistance when wet. The module runs at 5V.
  YL-83 Rain Sensor - Control Board: The YL-83 is a rain sensor that has more resistance when dry and less resistance when wet. The module runs at 5V.
  DFRobot Capacitive Soil Moisture Sensor V1.0: DFRobot Capacitive Soil Moisture Sensor V1.0 This product measures soil moisture levels by capacitive sensing, rather than resistive sensing like other types of moisture sensor. It is made of a corrosion resistant material giving it a long service life. Insert it into soil and impress your friends with the real-time soil moisture data! The product includes an on-board voltage regulator which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
