# Fritzing sketch design-moisture (saved by Fritzing 0.9.6b)

parts:
  Part1 = Arduino Uno (Rev3)
  Capacitive_Soil_Moisture_Sensor1 = DFRobot Capacitive Soil Moisture Sensor V1.0 [part_number=SEN0193]

nets:
  N1: Part1.A3, Capacitive_Soil_Moisture_Sensor1.A
  3V3: Part1.3V3, Capacitive_Soil_Moisture_Sensor1.VCC
  GND: Part1.GND, Capacitive_Soil_Moisture_Sensor1.GND

custom parts:
  DFRobot Capacitive Soil Moisture Sensor V1.0: DFRobot Capacitive Soil Moisture Sensor V1.0 This product measures soil moisture levels by capacitive sensing, rather than resistive sensing like other types of moisture sensor. It is made of a corrosion resistant material giving it a long service life. Insert it into soil and impress your friends with the real-time soil moisture data! The product includes an on-board voltage regulator which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
