# Fritzing sketch design-mq135 (saved by Fritzing 0.9.6b)
breadboards: 1

parts:
  RHT2 = Humidity and Temperature Sensor RHT03
  R2 = Resistor [tolerance=±5% resistance=10k package="0603 [SMD]"]
  Part1 = Arduino Uno (Rev3)
  Part2 = MQ-7 breakout

nets:
  VCC: RHT2.Vcc, R2.Pin_0, Part1.5V, Part2.VCC
  N1: RHT2.Data-signal, R2.Pin_1, Part1.D7
  GND: RHT2.GND_2, Part1.GND, Part2.GND
  N2: Part1.A0, Part2.AO

notes:
  MQ-135

custom parts:
  MQ-7 breakout: SKU: 101282
