# Fritzing sketch design-mq7 (saved by Fritzing 0.9.6b)
breadboards: 1

parts:
  Part1 = Arduino Uno (Rev3)
  Part2 = MQ-7 breakout

nets:
  N1: Part1.A1, Part2.AO
  5V: Part1.5V, Part2.VCC
  GND: Part1.GND, Part2.GND

custom parts:
  MQ-7 breakout: SKU: 101282
