# Fritzing sketch design-raindrop (saved by Fritzing 0.9.6b)
breadboards: 1

parts:
  Part1 = Arduino Uno (Rev3)
  YL-83_-_Detection_Board1 = YL-83 Rain Sensor - Detection Board
  YL-83_-_Control_Board1 = YL-83 Rain Sensor - Control Board

nets:
  N1: Part1.A2, YL-83_-_Control_Board1.AO
  5V: Part1.5V, YL-83_-_Control_Board1.VCC
  GND: Part1.GND, YL-83_-_Control_Board1.GND
  N2: YL-83_-_Detection_Board1.POS, YL-83_-_Control_Board1.POS
  N3: YL-83_-_Detection_Board1.NEG, YL-83_-_Control_Board1.NEG

custom parts:
  YL-83 Rain Sensor - Detection Board: The YL-83 is a rain sensor that has more resistance when dry and less resistance when wet. The module runs at 5V.
  YL-83 Rain Sensor - Control Board: The YL-83 is a rain sensor that has more resistance when dry and less resistance when wet. The module runs at 5V.
